# Fritzing sketch pi-lamp (saved by Fritzing 0.9.3b)

parts:
  Raspberry_Pi_Zero1 = Raspberry Pi Zero
  S4 = Round Pushbutton
  S5 = Round Pushbutton

nets:
  N1: Raspberry_Pi_Zero1.GPIO5, S4.leg0
  N2: Raspberry_Pi_Zero1.GPIO13, S5.leg1
  N3: Raspberry_Pi_Zero1.GND, S4.leg1, S5.leg0
